// Logisim project cpu.circ as structural Verilog: 7 circuits, main circuit main
// CPU
module main (
  input  [31:0] RS_READ_VALUE,
  input  [31:0] RI_READ_VALUE,
  input  [31:0] RD_READ_VALUE,
  input  [31:0] JC_READ_VALUE,
  input  [31:0] INSTRUCTION,
  input  TEMP_JUMPENABLE,
  input  CLOCK,
  output [4:0] RS,
  output [4:0] RI,
  output [4:0] RD,
  output [31:0] RD_WRITE_VALUE,
  output RD_WRITE_ENABLE,
  output [23:0] FETCH_ADDRESS
);

  wire IMMEDIATEMUX, u_decode_1_immediateflag;
  wire [2:0] u_decode_1_jc;
  wire [3:0] OPCODE, u_decode_1_opcode;
  wire [4:0] u_decode_1_rd, u_decode_1_ri, u_decode_1_rs;
  wire [16:0] u_decode_1_imm;
  wire [23:0] u_decode_1_addr;
  wire [31:0] IMM, multiplexer_1_out;

  u_PC u_pc_1 (.JUMPENABLE(TEMP_JUMPENABLE), .CLOCK(CLOCK), .PC(FETCH_ADDRESS));  // open: JUMPADDR
  Multiplexer #(.width(32)) multiplexer_1 (
    .in0(IMM), .in1(RI_READ_VALUE), .out(multiplexer_1_out), .sel(IMMEDIATEMUX));  // open: en
  u_DECODE u_decode_1 (
    .INSTRUCTION(INSTRUCTION), .OPCODE(u_decode_1_opcode), .IMMEDIATEFLAG(u_decode_1_immediateflag),
    .RD(u_decode_1_rd), .RS(u_decode_1_rs), .RI(u_decode_1_ri), .IMM(u_decode_1_imm), .JC(u_decode_1_jc),
    .ADDR(u_decode_1_addr));
  u_CONTROL u_control_1 (
    .OPCODE(u_decode_1_opcode), .IMMEDIATEFLAG(u_decode_1_immediateflag), .RD(u_decode_1_rd),
    .RS(u_decode_1_rs), .RI(u_decode_1_ri), .IMM(u_decode_1_imm), .JC(u_decode_1_jc), .ADDR(u_decode_1_addr),
    .OPCODE_2(OPCODE), .IMMEDIATEMUX(IMMEDIATEMUX), .RD_2(RD), .RS_2(RS), .RI_2(RI), .IMM_2(IMM));
  u_ALU u_alu_1 (.ALU_X(RS_READ_VALUE), .ALU_Y(multiplexer_1_out), .ALU_CONTROL(OPCODE));  // open: ALU_RESULT
  u_MEM u_mem_1 ();  // open: ADDRESS, WORD_MODE, MEM_WRITE, DATA_IN, CLOCK, DATA_OUT

  // Other names for the same wires on the sheet: FETCHPC[23:0] = FETCH_ADDRESS

  // Notes on the sheet:
  //   This is here as a placeholder until we actually implement jump conditions
  //   Feel free to use these ALU/MEM components, or delete them!
endmodule

module u_ALU (
  input  [31:0] ALU_X,
  input  [31:0] ALU_Y,
  output [31:0] ALU_RESULT,
  output [3:0] ALU_CONTROL
);

  u_REV u_rev_1 ();  // open: INPUT, REVERSE_AMOUNT, OUTPUT

  // Notes on the sheet:
  //   Feel free to use this component, or not, however you want!
endmodule

// Data Memory
module u_MEM (
  input  [24:0] ADDRESS,
  input  WORD_MODE,
  input  MEM_WRITE,
  input  [31:0] DATA_IN,
  input  CLOCK,
  output [31:0] DATA_OUT
);


  // Notes on the sheet:
  //   Feel free to use this component, or not, however you want!
  //   You might use the word mode input to differentiate LW/SW from LH/SH.
  //   However, you *SHOULD* use 2 RAM modules, one for even addresses and one for odd addresses.
endmodule

module u_REV (
  input  [31:0] INPUT,
  input  [4:0] REVERSE_AMOUNT,
  output [31:0] OUTPUT
);


  // Notes on the sheet:
  //   Feel free to use this component, or not, however you want!
endmodule

module u_DECODE (
  input  [31:0] INSTRUCTION,
  output [3:0] OPCODE,
  output IMMEDIATEFLAG,
  output [4:0] RD,
  output [4:0] RS,
  output [4:0] RI,
  output [16:0] IMM,
  output [2:0] JC,
  output [23:0] ADDR
);


  assign ADDR = INSTRUCTION[23:0];
  assign IMM = INSTRUCTION[16:0];
  assign IMMEDIATEFLAG = INSTRUCTION[27];
  assign JC = INSTRUCTION[26:24];
  assign OPCODE = INSTRUCTION[31:28];
  assign RD = INSTRUCTION[26:22];
  assign RI = INSTRUCTION[4:0];
  assign RS = INSTRUCTION[21:17];

  // Other names for the same wires on the sheet: ADDRT[23:0] = INSTRUCTION[23:0];
  //   IMMEDIATET[16:0] = INSTRUCTION[16:0]; INSTRUCT[31:0] = INSTRUCTION; RIT[4:0] = INSTRUCTION[4:0];
  //   RST[4:0] = INSTRUCTION[21:17]; RDT[4:0] = INSTRUCTION[26:22]; JCT[2:0] = INSTRUCTION[26:24];
  //   IMMEDIATEFLAGT = INSTRUCTION[27]; OPCODET[3:0] = INSTRUCTION[31:28]
endmodule

module u_CONTROL (
  input  [3:0] OPCODE,
  input  IMMEDIATEFLAG,
  input  [4:0] RD,
  input  [4:0] RS,
  input  [4:0] RI,
  input  [16:0] IMM,
  input  [2:0] JC,
  input  [23:0] ADDR,
  output [3:0] OPCODE_2,
  output IMMEDIATEMUX,
  output [4:0] RD_2,
  output [4:0] RS_2,
  output [4:0] RI_2,
  output [31:0] IMM_2
);


  assign IMM_2 = {{15{1'b0}}, IMM};
  assign IMMEDIATEMUX = IMMEDIATEFLAG;
  assign OPCODE_2 = OPCODE;
  assign RD_2 = RD;
  assign RI_2 = RI;
  assign RS_2 = RS;

  // Notes on the sheet:
  //   Very Simple for now. Only considering R-Type instructions
endmodule

module u_PC (
  input  JUMPENABLE,
  input  [23:0] JUMPADDR,
  input  CLOCK,
  output [23:0] PC
);

  wire [23:0] multiplexer_1_out, NEXTPC;

  Multiplexer #(.width(24)) multiplexer_1 (
    .in0(NEXTPC), .in1(JUMPADDR), .out(multiplexer_1_out), .sel(JUMPENABLE));  // open: en
  Register #(.width(24)) u_PC (.D(multiplexer_1_out), .Q(PC), .clk(CLOCK));  // open: en, clr
  Adder #(.width(24)) adder_1 (.a(24'h1), .b(PC), .out(NEXTPC));  // open: cin, cout
endmodule
